// Logisim project Lab 5 .circ as structural Verilog: 2 circuits, main circuit main
module main (
  input  [15:0] in_1,
  input  [3:0] in_2,
  input  [3:0] Write_Bits,
  input  [3:0] in_4,
  input  in_5,
  input  Clock,
  input  Reset,
  output [15:0] out_8,
  output [15:0] out_9
);

  wire and_1_out, and_2_out, and_3_out, and_4_out, and_5_out, and_6_out, and_7_out, and_8_out, and_9_out,
       and_10_out, and_11_out, and_12_out, and_13_out, and_14_out, and_15_out, and_16_out, decoder_1_out0,
       decoder_1_out1, decoder_1_out2, decoder_1_out3, decoder_1_out4, decoder_1_out5, decoder_1_out6,
       decoder_1_out7, decoder_1_out8, decoder_1_out9, decoder_1_out10, decoder_1_out11, decoder_1_out12,
       decoder_1_out13, decoder_1_out14, decoder_1_out15;
  wire [15:0] _1_q, _2_q, _3_q, _4_q, _5_q, _6_q, _7_q, _8_q, _9_q, _10_q, _11_q, _12_q, _13_q, _14_q, _15_q,
       _16_q;

  Decoder #(.select(4)) decoder_1 (
    .out0(decoder_1_out0), .out1(decoder_1_out1), .out2(decoder_1_out2), .out3(decoder_1_out3),
    .out4(decoder_1_out4), .out5(decoder_1_out5), .out6(decoder_1_out6), .out7(decoder_1_out7),
    .out8(decoder_1_out8), .out9(decoder_1_out9), .out10(decoder_1_out10), .out11(decoder_1_out11),
    .out12(decoder_1_out12), .out13(decoder_1_out13), .out14(decoder_1_out14), .out15(decoder_1_out15),
    .sel(Write_Bits));  // open: en
  and and_1 (and_1_out, decoder_1_out0, in_5);
  and and_2 (and_2_out, decoder_1_out1, in_5);
  and and_3 (and_3_out, decoder_1_out2, in_5);
  and and_4 (and_4_out, decoder_1_out3, in_5);
  and and_5 (and_5_out, decoder_1_out4, in_5);
  and and_6 (and_6_out, decoder_1_out5, in_5);
  and and_7 (and_7_out, decoder_1_out6, in_5);
  and and_8 (and_8_out, decoder_1_out7, in_5);
  and and_9 (and_9_out, decoder_1_out8, in_5);
  and and_10 (and_10_out, decoder_1_out9, in_5);
  and and_11 (and_11_out, decoder_1_out10, in_5);
  and and_12 (and_12_out, decoder_1_out11, in_5);
  and and_13 (and_13_out, decoder_1_out12, in_5);
  and and_14 (and_14_out, decoder_1_out13, in_5);
  and and_15 (and_15_out, decoder_1_out14, in_5);
  and and_16 (and_16_out, decoder_1_out15, in_5);
  Register #(.width(16)) _1 (.D(in_1), .en(and_1_out), .Q(_1_q), .clk(Clock), .clr(Reset));
  Register #(.width(16)) _2 (.D(in_1), .en(and_2_out), .Q(_2_q), .clk(Clock), .clr(Reset));
  Register #(.width(16)) _3 (.D(in_1), .en(and_3_out), .Q(_3_q), .clk(Clock), .clr(Reset));
  Register #(.width(16)) _4 (.D(in_1), .en(and_4_out), .Q(_4_q), .clk(Clock), .clr(Reset));
  Register #(.width(16)) _5 (.D(in_1), .en(and_5_out), .Q(_5_q), .clk(Clock), .clr(Reset));
  Register #(.width(16)) _6 (.D(in_1), .en(and_6_out), .Q(_6_q), .clk(Clock), .clr(Reset));
  Register #(.width(16)) _7 (.D(in_1), .en(and_7_out), .Q(_7_q), .clk(Clock), .clr(Reset));
  Register #(.width(16)) _8 (.D(in_1), .en(and_8_out), .Q(_8_q), .clk(Clock), .clr(Reset));
  Register #(.width(16)) _9 (.D(in_1), .en(and_9_out), .Q(_9_q), .clk(Clock), .clr(Reset));
  Register #(.width(16)) _10 (.D(in_1), .en(and_10_out), .Q(_10_q), .clk(Clock), .clr(Reset));
  Register #(.width(16)) _11 (.D(in_1), .en(and_11_out), .Q(_11_q), .clk(Clock), .clr(Reset));
  Register #(.width(16)) _12 (.D(in_1), .en(and_12_out), .Q(_12_q), .clk(Clock), .clr(Reset));
  Register #(.width(16)) _13 (.D(in_1), .en(and_13_out), .Q(_13_q), .clk(Clock), .clr(Reset));
  Register #(.width(16)) _14 (.D(in_1), .en(and_14_out), .Q(_14_q), .clk(Clock), .clr(Reset));
  Register #(.width(16)) _15 (.D(in_1), .en(and_15_out), .Q(_15_q), .clk(Clock), .clr(Reset));
  Register #(.width(16)) _16 (.D(in_1), .en(and_16_out), .Q(_16_q), .clk(Clock), .clr(Reset));
  Multiplexer #(.select(4), .width(16)) multiplexer_1 (
    .in0(_1_q), .in1(_2_q), .in2(_3_q), .in3(_4_q), .in4(_5_q), .in5(_6_q), .in6(_7_q), .in7(_8_q),
    .in8(_9_q), .in9(_10_q), .in10(_11_q), .in11(_12_q), .in12(_13_q), .in13(_14_q), .in14(_15_q),
    .in15(_16_q), .out(out_8), .sel(in_2));  // open: en
  Multiplexer #(.select(4), .width(16)) multiplexer_2 (
    .in0(_1_q), .in1(_2_q), .in2(_3_q), .in3(_4_q), .in4(_5_q), .in5(_6_q), .in6(_7_q), .in7(_8_q),
    .in8(_9_q), .in9(_10_q), .in10(_11_q), .in11(_12_q), .in12(_13_q), .in13(_14_q), .in14(_15_q),
    .in15(_16_q), .out(out_9), .sel(in_4));  // open: en

  // Notes on the sheet:
  //   Write Data
  //   Register Write Control Signal
  //   Rs=Rd=Rt=4,Register 16, Data bit 16 (ALU 16 bits)
  //   Read Register1
  //   Read Register2
  //   Read  Data1
  //   Read  Data2
endmodule

module _16_bit_register_file (
  input  [15:0] in_1,
  input  [3:0] in_2,
  input  [3:0] RD,
  input  [3:0] in_4,
  input  in_5,
  input  Clock,
  input  Reset,
  output [15:0] out_8,
  output [15:0] out_9
);

  wire and_1_out, and_2_out, and_3_out, and_4_out, and_5_out, and_6_out, and_7_out, and_8_out, and_9_out,
       and_10_out, and_11_out, and_12_out, and_13_out, and_14_out, and_15_out, and_16_out, decoder_1_out0,
       decoder_1_out1, decoder_1_out2, decoder_1_out3, decoder_1_out4, decoder_1_out5, decoder_1_out6,
       decoder_1_out7, decoder_1_out8, decoder_1_out9, decoder_1_out10, decoder_1_out11, decoder_1_out12,
       decoder_1_out13, decoder_1_out14, decoder_1_out15;
  wire [15:0] _1_q, _2_q, _3_q, _4_q, _5_q, _6_q, _7_q, _8_q, _9_q, _10_q, _11_q, _12_q, _13_q, _14_q, _15_q,
       _16_q, undriven;

  Decoder #(.select(4)) decoder_1 (
    .out0(decoder_1_out0), .out1(decoder_1_out1), .out2(decoder_1_out2), .out3(decoder_1_out3),
    .out4(decoder_1_out4), .out5(decoder_1_out5), .out6(decoder_1_out6), .out7(decoder_1_out7),
    .out8(decoder_1_out8), .out9(decoder_1_out9), .out10(decoder_1_out10), .out11(decoder_1_out11),
    .out12(decoder_1_out12), .out13(decoder_1_out13), .out14(decoder_1_out14), .out15(decoder_1_out15),
    .sel(RD));  // open: en
  and and_1 (and_1_out, decoder_1_out0, in_5);
  and and_2 (and_2_out, decoder_1_out1, in_5);
  and and_3 (and_3_out, decoder_1_out2, in_5);
  and and_4 (and_4_out, decoder_1_out3, in_5);
  and and_5 (and_5_out, decoder_1_out4, in_5);
  and and_6 (and_6_out, decoder_1_out5, in_5);
  and and_7 (and_7_out, decoder_1_out6, in_5);
  and and_8 (and_8_out, decoder_1_out7, in_5);
  and and_9 (and_9_out, decoder_1_out8, in_5);
  and and_10 (and_10_out, decoder_1_out9, in_5);
  and and_11 (and_11_out, decoder_1_out10, in_5);
  and and_12 (and_12_out, decoder_1_out11, in_5);
  and and_13 (and_13_out, decoder_1_out12, in_5);
  and and_14 (and_14_out, decoder_1_out13, in_5);
  and and_15 (and_15_out, decoder_1_out14, in_5);
  and and_16 (and_16_out, decoder_1_out15, in_5);
  Register #(.width(16)) _1 (.D(in_1), .en(and_1_out), .Q(_1_q), .clk(Clock), .clr(Reset));
  Register #(.width(16)) _2 (.D(in_1), .en(and_2_out), .Q(_2_q), .clk(Clock), .clr(Reset));
  Register #(.width(16)) _3 (.D(in_1), .en(and_3_out), .Q(_3_q), .clk(Clock), .clr(Reset));
  Register #(.width(16)) _4 (.D(in_1), .en(and_4_out), .Q(_4_q), .clk(Clock), .clr(Reset));
  Register #(.width(16)) _5 (.D(in_1), .en(and_5_out), .Q(_5_q), .clk(Clock), .clr(Reset));
  Register #(.width(16)) _6 (.D(in_1), .en(and_6_out), .Q(_6_q), .clk(Clock), .clr(Reset));
  Register #(.width(16)) _7 (.D(in_1), .en(and_7_out), .Q(_7_q), .clk(Clock), .clr(Reset));
  Register #(.width(16)) _8 (.D(in_1), .en(and_8_out), .Q(_8_q), .clk(Clock), .clr(Reset));
  Register #(.width(16)) _9 (.D(in_1), .en(and_9_out), .Q(_9_q), .clk(Clock), .clr(Reset));
  Register #(.width(16)) _10 (.D(in_1), .en(and_10_out), .Q(_10_q), .clk(Clock), .clr(Reset));
  Register #(.width(16)) _11 (.D(in_1), .en(and_11_out), .Q(_11_q), .clk(Clock), .clr(Reset));
  Register #(.width(16)) _12 (.D(in_1), .en(and_12_out), .Q(_12_q), .clk(Clock), .clr(Reset));
  Register #(.width(16)) _13 (.D(in_1), .en(and_13_out), .Q(_13_q), .clk(Clock), .clr(Reset));
  Register #(.width(16)) _14 (.D(in_1), .en(and_14_out), .Q(_14_q), .clk(Clock), .clr(Reset));
  Register #(.width(16)) _15 (.D(undriven), .en(and_15_out), .Q(_15_q), .clk(Clock), .clr(Reset));
  Register #(.width(16)) _16 (.D(undriven), .en(and_16_out), .Q(_16_q), .clk(Clock), .clr(Reset));
  Multiplexer #(.select(4), .width(16)) multiplexer_1 (
    .in0(_1_q), .in1(_2_q), .in2(_3_q), .in3(_4_q), .in4(_5_q), .in5(_6_q), .in6(_7_q), .in7(_8_q),
    .in8(_9_q), .in9(_10_q), .in10(_11_q), .in11(_12_q), .in12(_13_q), .in13(_14_q), .in14(_15_q),
    .in15(_16_q), .out(out_8), .sel(in_2));  // open: en
  Multiplexer #(.select(4), .width(16)) multiplexer_2 (
    .in0(_1_q), .in1(_2_q), .in2(_3_q), .in3(_4_q), .in4(_5_q), .in5(_6_q), .in6(_7_q), .in7(_8_q),
    .in8(_9_q), .in9(_10_q), .in10(_11_q), .in11(_12_q), .in12(_13_q), .in13(_14_q), .in14(_15_q),
    .in15(_16_q), .out(out_9), .sel(in_4));  // open: en

  // Notes on the sheet:
  //   Write Data
  //   Register Write
  //   Rs=Rd=Rt=4,Register 16, Data bit 16 (ALU 16 bits)
  //   RS
  //   RT
  //   Hossain Ahmmed
  //   2232102042
  //   Read  Data1
  //   Read  Data2
endmodule
