// Logisim project Lab 7_1 .circ as structural Verilog
// IF
module Instruction_Fetch_Unit (
  input  Clock,
  input  Clear,
  output [15:0] out_3
);

  wire [1:0] adder_1_out, register_1_q;

  Register #(.width(2)) register_1 (.D(adder_1_out), .Q(register_1_q), .clk(Clock), .clr(Clear));  // open: en
  Adder #(.width(2)) adder_1 (.a(2'b01), .b(register_1_q), .out(adder_1_out));  // open: cin, cout
  ROM #(.addrWidth(2), .dataWidth(16)) rom_1 (.addr(register_1_q), .data(out_3));  // open: sel

  // Notes on the sheet:
  //   16 bit ISA
  //   4 instruction
  //   contents of rom_1 (hex, n*v repeats v):
  //   2070 213a 313f
  //   Data
  //   Hossain Ahmmed Taufiq 
  //   2232102042
endmodule

module R_Type_Datapath (
  input  Clock,
  input  Clear,
  input  Register_Write,
  output [15:0] out_4,
  output [15:0] out_5
);

  wire [1:0] bit_extender_1_out;
  wire [15:0] n16_bit_register_file_1_out_8, n16_bit_register_file_1_out_9;

  Instruction_Fetch_Unit instruction_fetch_unit_1 (.Clock(Clock), .out_3(out_4));  // open: Clear
  _16_bit_register_file u_16_bit_register_file_1 (
    .in_1(out_5), .RD(out_4[3:0]), .in_5(Register_Write), .Clock(Clock),
    .out_8(n16_bit_register_file_1_out_8), .in_2(out_4[11:8]), .out_9(n16_bit_register_file_1_out_9),
    .in_4(out_4[7:4]), .Reset(Clear));
  Bit_Extender #(.in_width(4), .out_width(2)) bit_extender_1 (.in(out_4[15:12]), .out(bit_extender_1_out));
  _16_Bit_ALU u_16_bit_alu_1 (
    .in_2(n16_bit_register_file_1_out_8), .in_3(n16_bit_register_file_1_out_9), .OP_Code(bit_extender_1_out),
    .out_5(out_5));  // open: Cin, out_6, Cout

  // Notes on the sheet:
  //   Hossain Ahmmed Taufiq 
  //   2232102042
  //   ADD $t2,t0,t1 
  //   OP|RS|RT|RD
  //   0010 0110 0111 1000
endmodule

module ALU (
  input  Cin,
  input  [15:0] in_2,
  input  [15:0] in_3,
  input  [1:0] Select,
  output [15:0] out_5,
  output out_6,
  output Cout
);

  wire _1_cout, _2_cout, _3_cout, _4_cout, _5_cout, _6_cout, _7_cout, _8_cout, _9_cout, _10_cout, _11_cout,
       _12_cout, _13_cout, _14_cout, _15_cout;

  _1_Bit_ALU _1 (.Cin(Cin), .A(in_2[0]), .B(in_3[0]), .Select(Select), .Result(out_5[0]), .Cout(_1_cout));
  _1_Bit_ALU _2 (.Cin(_1_cout), .A(in_2[1]), .B(in_3[1]), .Select(Select), .Result(out_5[1]), .Cout(_2_cout));
  _1_Bit_ALU _3 (.Cin(_2_cout), .A(in_2[2]), .B(in_3[2]), .Select(Select), .Result(out_5[2]), .Cout(_3_cout));
  _1_Bit_ALU _4 (.Cin(_3_cout), .A(in_2[3]), .B(in_3[3]), .Select(Select), .Result(out_5[3]), .Cout(_4_cout));
  _1_Bit_ALU _5 (.Cin(_4_cout), .A(in_2[4]), .B(in_3[4]), .Select(Select), .Result(out_5[4]), .Cout(_5_cout));
  _1_Bit_ALU _6 (.Cin(_5_cout), .A(in_2[5]), .B(in_3[5]), .Select(Select), .Result(out_5[5]), .Cout(_6_cout));
  _1_Bit_ALU _7 (.Cin(_6_cout), .A(in_2[6]), .B(in_3[6]), .Select(Select), .Result(out_5[6]), .Cout(_7_cout));
  _1_Bit_ALU _8 (.Cin(_7_cout), .A(in_2[7]), .B(in_3[7]), .Select(Select), .Result(out_5[7]), .Cout(_8_cout));
  _1_Bit_ALU _9 (.Cin(_8_cout), .A(in_2[8]), .B(in_3[8]), .Select(Select), .Result(out_5[8]), .Cout(_9_cout));
  _1_Bit_ALU _10 (.Cin(_9_cout), .A(in_2[9]), .B(in_3[9]), .Select(Select), .Result(out_5[9]), .Cout(_10_cout));
  _1_Bit_ALU _11 (.Cin(_10_cout), .A(in_2[10]), .B(in_3[10]), .Select(Select), .Result(out_5[10]), .Cout(_11_cout));
  _1_Bit_ALU _12 (.Cin(_11_cout), .A(in_2[11]), .B(in_3[11]), .Select(Select), .Result(out_5[11]), .Cout(_12_cout));
  _1_Bit_ALU _13 (.Cin(_12_cout), .A(in_2[12]), .B(in_3[12]), .Select(Select), .Result(out_5[12]), .Cout(_13_cout));
  _1_Bit_ALU _14 (.Cin(_13_cout), .A(in_2[13]), .B(in_3[13]), .Select(Select), .Result(out_5[13]), .Cout(_14_cout));
  _1_Bit_ALU _15 (.Cin(_14_cout), .A(in_2[14]), .B(in_3[14]), .Select(Select), .Result(out_5[14]), .Cout(_15_cout));
  _1_Bit_ALU _16 (.Cin(_15_cout), .A(in_2[15]), .B(in_3[15]), .Select(Select), .Result(out_5[15]), .Cout(Cout));
  nor nor_1 (out_6, out_5[0], out_5[1], out_5[2], out_5[3], out_5[4], out_5[5], out_5[6], out_5[7], out_5[8], out_5[9], out_5[10], out_5[11], out_5[12], out_5[13], out_5[14], out_5[15]);

  // Notes on the sheet:
  //   A
  //   B
  //   Figure:16 Bit ALU
  //   Hossain Ahmmed Taufiq
  //   2232102042
  //   Result
  //   Zero signal
endmodule
