// Logisim project Lab6.circ as structural Verilog
module _1_Bit_ALU (
  input  Cin,
  input  A,
  input  B,
  input  [1:0] Select,
  output Result,
  output Cout
);

  wire adder_1_out, and_1_out, and_2_out, multiplexer_1_out, not_1_out, or_1_out;

  not not_1 (not_1_out, B);
  Multiplexer multiplexer_1 (.in0(B), .in1(not_1_out), .out(multiplexer_1_out), .sel(and_1_out));  // open: en
  and and_1 (and_1_out, Select[0], Select[1]);
  and and_2 (and_2_out, A, B);
  or or_1 (or_1_out, A, B);
  Adder #(.width(1)) adder_1 (.a(A), .b(multiplexer_1_out), .out(adder_1_out), .cin(Cin), .cout(Cout));
  Multiplexer #(.select(2)) multiplexer_2 (
    .in0(and_2_out), .in1(or_1_out), .in2(adder_1_out), .in3(adder_1_out), .out(Result), .sel(Select));  // open: en

  // Notes on the sheet:
  //   Figure:1Bit ALU
  //   Maymuna Khanom
  //   2232039642
endmodule

module _16_Bit_ALU (
  input  Cin,
  input  [15:0] in_2,
  input  [15:0] in_3,
  input  [1:0] OP_Code,
  output [15:0] out_5,
  output out_6,
  output Cout
);

  wire _1_cout, _2_cout, _3_cout, _4_cout, _5_cout, _6_cout, _7_cout, _8_cout, _9_cout, _10_cout, _11_cout,
       _12_cout, _13_cout, _14_cout, _15_cout;

  _1_Bit_ALU _1 (.Cin(Cin), .A(in_2[0]), .B(in_3[0]), .Select(OP_Code), .Result(out_5[0]), .Cout(_1_cout));
  _1_Bit_ALU _2 (.Cin(_1_cout), .A(in_2[1]), .B(in_3[1]), .Select(OP_Code), .Result(out_5[1]), .Cout(_2_cout));
  _1_Bit_ALU _3 (.Cin(_2_cout), .A(in_2[2]), .B(in_3[2]), .Select(OP_Code), .Result(out_5[2]), .Cout(_3_cout));
  _1_Bit_ALU _4 (.Cin(_3_cout), .A(in_2[3]), .B(in_3[3]), .Select(OP_Code), .Result(out_5[3]), .Cout(_4_cout));
  _1_Bit_ALU _5 (.Cin(_4_cout), .A(in_2[4]), .B(in_3[4]), .Select(OP_Code), .Result(out_5[4]), .Cout(_5_cout));
  _1_Bit_ALU _6 (.Cin(_5_cout), .A(in_2[5]), .B(in_3[5]), .Select(OP_Code), .Result(out_5[5]), .Cout(_6_cout));
  _1_Bit_ALU _7 (.Cin(_6_cout), .A(in_2[6]), .B(in_3[6]), .Select(OP_Code), .Result(out_5[6]), .Cout(_7_cout));
  _1_Bit_ALU _8 (.Cin(_7_cout), .A(in_2[7]), .B(in_3[7]), .Select(OP_Code), .Result(out_5[7]), .Cout(_8_cout));
  _1_Bit_ALU _9 (.Cin(_8_cout), .A(in_2[8]), .B(in_3[8]), .Select(OP_Code), .Result(out_5[8]), .Cout(_9_cout));
  _1_Bit_ALU _10 (.Cin(_9_cout), .A(in_2[9]), .B(in_3[9]), .Select(OP_Code), .Result(out_5[9]), .Cout(_10_cout));
  _1_Bit_ALU _11 (.Cin(_10_cout), .A(in_2[10]), .B(in_3[10]), .Select(OP_Code), .Result(out_5[10]), .Cout(_11_cout));
  _1_Bit_ALU _12 (.Cin(_11_cout), .A(in_2[11]), .B(in_3[11]), .Select(OP_Code), .Result(out_5[11]), .Cout(_12_cout));
  _1_Bit_ALU _13 (.Cin(_12_cout), .A(in_2[12]), .B(in_3[12]), .Select(OP_Code), .Result(out_5[12]), .Cout(_13_cout));
  _1_Bit_ALU _14 (.Cin(_13_cout), .A(in_2[13]), .B(in_3[13]), .Select(OP_Code), .Result(out_5[13]), .Cout(_14_cout));
  _1_Bit_ALU _15 (.Cin(_14_cout), .A(in_2[14]), .B(in_3[14]), .Select(OP_Code), .Result(out_5[14]), .Cout(_15_cout));
  _1_Bit_ALU _16 (.Cin(_15_cout), .A(in_2[15]), .B(in_3[15]), .Select(OP_Code), .Result(out_5[15]), .Cout(Cout));
  nor nor_1 (out_6, out_5[0], out_5[1], out_5[2], out_5[3], out_5[4], out_5[5], out_5[6], out_5[7], out_5[8], out_5[9], out_5[10], out_5[11], out_5[12], out_5[13], out_5[14], out_5[15]);

  // Notes on the sheet:
  //   Data 1
  //   Data 2
  //   Figure:16 Bit ALU
  //   Hossain Ahmmed Taufiq 
  //   2232102042
  //   Result
  //   Zero signal
endmodule
