// Logisim project lab_7_02.circ as structural Verilog
module Data_Memory (
  input  [1:0] Address,
  input  [15:0] Data,
  input  Mem_Write,
  input  MemRead,
  input  Clock,
  output [15:0] Output
);

  RAM #(.addrWidth(2), .dataWidth(16), .bus("separate")) ram_1 (
    .addr(Address), .din(Data), .data(Output), .str(Mem_Write), .clk(Clock), .ld(MemRead));  // open: sel, clr
endmodule

module I_Type_Data_Path (
  input  Mem_Write,
  input  Clock,
  input  MemRead,
  input  Clear,
  input  Register_Write,
  output [15:0] Data,
  output [15:0] out_7,
  output [15:0] out_8,
  output [1:0] Address,
  output [15:0] Output,
  output [15:0] out_11,
  output [15:0] out_12
);

  wire [1:0] adder_1_out, bit_extender_1_out, register_1_q;

  Register #(.width(2)) register_1 (.D(adder_1_out), .Q(register_1_q), .clk(Clock), .clr(Clear));  // open: en
  Adder #(.width(2)) adder_1 (.a(register_1_q), .b(2'b01), .out(adder_1_out));  // open: cin, cout
  ROM #(.addrWidth(2), .dataWidth(16)) rom_1 (.addr(register_1_q), .data(Data));  // open: sel
  _16_bit_register_file u_16_bit_register_file_1 (
    .in_1(Output), .RD(Data[7:4]), .in_5(Register_Write), .Clock(Clock), .out_8(out_7), .in_2(Data[11:8]),
    .out_9(out_11), .in_4(Data[7:4]), .Reset(Clear));
  Bit_Extender #(.in_width(4), .out_width(2)) bit_extender_1 (.in(Data[15:12]), .out(bit_extender_1_out));
  assign out_12 = {{12{1'b0}}, Data[3:0]};  // Bit_Extender bit_extender_2
  _16_Bit_ALU u_16_bit_alu_1 (
    .in_2(out_7), .in_3(out_12), .OP_Code(bit_extender_1_out), .out_5(out_8));  // open: Cin, out_6, Cout
  Bit_Extender #(.in_width(16), .out_width(2)) bit_extender_3 (.in(out_8), .out(Address));
  RAM #(.addrWidth(2), .dataWidth(16), .bus("separate")) ram_1 (
    .addr(Address), .din(out_11), .data(Output), .str(Mem_Write), .clk(Clock), .ld(MemRead), .clr(Clear));  // open: sel

  // Notes on the sheet:
  //   contents of rom_1 (hex, n*v repeats v):
  //   2061 2063
  //   OP|RS| RD|Im
  //   lw $t0, 1($zero)
  //   0010 0000 0110 0001
  //   sw $t0, 0($Zero)
  //   0010 0000 0110 0000
  //   OP|RS| RT|Im
  //   Hexa-2061
  //   Hexa-2060
  //   Hossain  Ahmmed Taufiq 
endmodule
